# Fritzing sketch logical_schematic (saved by Fritzing 0.9.6b)
breadboards: 2

parts:
  U1 = ESP32S-HiLetgo [part_number=ESP32S-HiLetgo]
  Part1 = BME280 Breakout
  R1 = Resistor [tolerance=±5% resistance=3.3k power=0.25 package=THT]
  R2 = Resistor [tolerance=±5% resistance=3.3k power=0.25 package=THT]
  R3 = Resistor [tolerance=±5% resistance=10k power=0.25 package=THT]
  R4 = Resistor [tolerance=±5% resistance=3.3k power=0.25 package=THT]
  PWM_Fan_(x2) = Fan - 4 wire [package=THT]
  C1 = Ceramic Capacitor [capacitance=0.1nF package="100 mil [THT, multilayer]"]

nets:
  N1: U1.3.3, Part1.3.3V, R3.Pin_1
  GND: U1.GND, Part1.GND, PWM_Fan_(x2).GND, C1.1
  N2: U1.GPIO21, Part1.SDI/SDA, R2.Pin_0
  N3: U1.GPIO22, Part1.SCK/SCL, R1.Pin_0
  N4: R3.Pin_0, R4.Pin_0
  N5: R4.Pin_1, C1.0

notes:
  3.3 VCC
  I2C
  12 VCC

custom parts:
  ESP32S-HiLetgo: HiLetgo ESP-WROOM-32 ESP32 ESP-32S Development Board 2.4GHz Dual-Mode WiFi + Bluetooth Dual Cores Microcontroller The ESP32 integrated with Antenna switches, RF Balun, power amplifiers, low-noise amplifiers, filters, and management modules, and the entire solution occupies the least area of PCB. 2.4 GHz Wi-Fi plus Bluetooth dual-mode chip, with TSMC Ultra-low power consumption 40nm technology,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
  Fan - 4 wire: Fan, 4 wire with tach.
